# Fritzing sketch door_closer (saved by Fritzing 0.9.4)
circuit board: 8.46667cm x 5.64444cm
breadboards: 1

parts:
  U1 = NodeMCU V1.0
  OMRON1 = OMRON PCB Power Relay – G5LE [part_number="G5LE-1\n" package=THT]
  Q1 = npn-Powertransistor [package="TO220 [THT]"]
  R1 = Resistor [tolerance=±5% resistance=220 package="1206 [SMD]"]
  SG1 = Buzzer 12mm [package=buzzer-12mm-ns-kit]
  HC-SR04_Sensor_1 = HC-SR04 Ultrasonic Distance Sensor

nets (from the schematic view):
  N1: U1.D2, HC-SR04_Sensor_1.GND
  N2: U1.D3, HC-SR04_Sensor_1.TRIG
  N3: U1.D4, SG1.1
  N4: U1.3V3, OMRON1.COIL1
  N5: U1.GND, Q1.emitter, SG1.2, HC-SR04_Sensor_1.ECHO
  N6: U1.D7, R1.Pin_0
  VIN: U1.Vin, HC-SR04_Sensor_1.VCC
  N7: OMRON1.COIL2, Q1.collector
  N8: Q1.base, R1.Pin_1

custom parts:
  NodeMCU V1.0: ESP8266 based NodeMCU
